# Fritzing sketch Halloween_Skull (saved by Fritzing 0.9.3b)
breadboards: 1

parts:
  Bauteil1 = Arduino Uno (Rev3) - ICSP
  hc-sr1 = hc-sr04
  LED2 = smd LED [color="Red (633nm)" package="1206 [SMD]"]
  LED3 = smd LED [color="Red (633nm)" package="1206 [SMD]"]
  R1 = Resistor [tolerance=±5% resistance=100 package="1206 [SMD]"]

nets:
  N1: Bauteil1.D12/MISO, hc-sr1.Trig
  N2: Bauteil1.D13/SCK, hc-sr1.Echo
  GND: Bauteil1.GND, hc-sr1.GND, R1.Pin_1
  N3: Bauteil1.D5_PWM, LED2.anode
  N4: Bauteil1.D6_PWM, LED3.anode
  5V: Bauteil1.5V, hc-sr1.VCC
  N5: LED2.cathode, LED3.cathode, R1.Pin_0
